// Logisim project oven.circ as structural Verilog: 3 circuits, main circuit main
module main (
  input  in_onoff,
  input  in_sensor,
  input  rst,
  output out_warn,
  output out_on,
  output out_ready
);

  wire and_2_out, and_3_out, and_4_out, clock_1_out, d0_logic_1_d0, d1_logic_1_d1, not_1_out, not_2_out, Q0_q;

  Clock clock_1 (.out(clock_1_out));
  D_Flip_Flop Q0 (.D(d0_logic_1_d0), .clk(clock_1_out), .Q(Q0_q), .reset(rst));  // open: Qn, preset
  D0_logic d0_logic_1 (.Q1(out_ready), .Q0(Q0_q), .in_sensor(in_sensor), .in_onoff(in_onoff), .D0(d0_logic_1_d0));
  not not_1 (not_1_out, Q0_q);
  D_Flip_Flop Q1 (.D(d1_logic_1_d1), .clk(clock_1_out), .Q(out_ready), .reset(rst));  // open: Qn, preset
  not not_2 (not_2_out, out_ready);
  D1_logic d1_logic_1 (.Q1(out_ready), .Q0(Q0_q), .in_sensor(in_sensor), .in_onoff(in_onoff), .D1(d1_logic_1_d1));
  and and_1 (out_warn, out_ready, in_sensor, Q0_q);
  and and_2 (and_2_out, not_1_out, out_ready);
  and and_3 (and_3_out, not_2_out, Q0_q);
  and and_4 (and_4_out, Q0_q, out_ready);
  or or_1 (out_on, and_2_out, and_3_out, and_4_out);
endmodule

module D1_logic (
  input  Q1,
  input  Q0,
  input  in_sensor,
  input  in_onoff,
  output D1
);

  wire and5_out, and7_out, and9_out, and11_out, and13_out, not_1_out, not_2_out, not_3_out, not_4_out;

  not not_1 (not_1_out, Q1);
  not not_2 (not_2_out, Q0);
  not not_3 (not_3_out, in_sensor);
  not not_4 (not_4_out, in_onoff);
  and and5 (and5_out, not_1_out, Q0, not_3_out, not_4_out);
  and and7 (and7_out, not_1_out, Q0, in_sensor, not_4_out);
  and and9 (and9_out, Q1, not_2_out, not_3_out, not_4_out);
  and and11 (and11_out, Q1, not_2_out, in_sensor, not_4_out);
  and and13 (and13_out, Q1, Q0, not_3_out, not_4_out);
  or finalOR (D1, and5_out, and7_out, and9_out, and11_out, and13_out);
endmodule

module D0_logic (
  input  Q1,
  input  Q0,
  input  in_sensor,
  input  in_onoff,
  output D0
);

  wire and2_out, and4_out, and7_out, and11_out, not_1_out, not_2_out, not_3_out, not_4_out;

  not not_1 (not_1_out, Q1);
  not not_2 (not_2_out, Q0);
  not not_3 (not_3_out, in_sensor);
  not not_4 (not_4_out, in_onoff);
  and and2 (and2_out, not_1_out, not_2_out, not_3_out, in_onoff);
  and and4 (and4_out, not_1_out, not_2_out, in_sensor, in_onoff);
  and and7 (and7_out, not_1_out, Q0, in_sensor, not_4_out);
  and and11 (and11_out, Q1, not_2_out, in_sensor, not_4_out);
  or or_1 (D0, and2_out, and4_out, and7_out, and11_out);
endmodule
